# Fritzing sketch initial-design (saved by Fritzing 0.9.6b)

parts:
  Part1 = Arduino Uno (Rev3) - ICSP
  M1 = Dagu DGServo 9g (End View) [part_number=RS001B]
  S1 = H-Bridge with L298N
  Part2 = SRF05 Ultrasonic Rangefinder
  M3 = DC Motor
  M2 = DC Motor
  VCC1 = 4 x AAA Battery Mount
  Part3 = IR Receiver Breakout [package=PCB]

nets:
  N1: Part1.ICSP_MOSI, Part1.D11_PWM/MOSI, S1.ENA
  N2: Part1.D8, Part2.Echo
  N3: Part1.D9_PWM, S1.IN4
  N4: Part1.D10_PWM/SS, S1.IN3
  GND: Part1.GND, M1.gnd, S1.GND, Part2.GND, VCC1.-, Part3.GND
  N5: Part1.D2, Part3.OUT
  N6: Part1.D3_PWM, S1.ENB
  N7: Part1.D4, S1.IN2
  N8: Part1.D5_PWM, M1.pulse
  N9: Part1.D6_PWM, S1.IN1
  N10: Part1.D7, Part2.Trig
  VCC: Part1.5V, M1.vcc, Part2.VCC, Part3.VCC
  VIN: Part1.VIN, S1.5V
  N11: S1.12V, VCC1.+
  N12: S1.M1-01, M3.pin_2
  N13: S1.M1-02, M3.pin_1
  N14: S1.M2-01, M2.pin_2
  N15: S1.M2-02, M2.pin_1

custom parts:
  H-Bridge with L298N: h-bridge
